# Fritzing sketch ESP8266_ESP_12E_webserver (saved by Fritzing 0.9.4)
breadboards: 1

parts:
  LED1 = LED - 3mm [color="Red (633nm)" package="3 mm [THT]"]
  LED2 = LED - 3mm [color="Green (555nm)" package="3 mm [THT]"]
  U1 = ESP8266 NodeMCU LoLin module
  R1 = Resistor [tolerance=±5% resistance=220 package="0402 [SMD]"]
  R2 = Resistor [tolerance=±5% resistance=220 package="0402 [SMD]"]

nets:
  N1: LED1.cathode, R1.Pin_1
  N2: LED1.anode, U1.D1
  N3: LED2.cathode, R2.Pin_1
  N4: LED2.anode, U1.D2
  N5: U1.GND, R1.Pin_0, R2.Pin_0

custom parts:
  ESP8266 NodeMCU LoLin module: ESP8266 based NodeMCU
